# Fritzing sketch 20 (saved by Fritzing 0.9.3b)
breadboards: 1

parts:
  hc-sr1 = hc-sr04
  hc-sr2 = hc-sr04
  hc-sr3 = hc-sr04
  Componente1 = Arduino Mega 2560 (Rev3)
  J1 = Basic Servo
  IC1 = L293D [package=THT]
  DC_Mot_Enc2 = DC Motor with two-phase hall-encoder [part_number=VT-E-G25A-06-177E]
  VCC2 = Battery
  U1 = TRANSCHIPTC5747 [package=camera_sfv24r-2st_2]  # not connected
  U2 = TRANSCHIPTC5747 [package=camera_sfv24r-2st_2]  # not connected
  U3 = TRANSCHIPTC5747 [package=camera_sfv24r-2st_2]  # not connected

nets:
  VCC: hc-sr1.VCC, hc-sr2.VCC, hc-sr3.VCC, Componente1.5V, J1.vcc, IC1.+Vmotor, DC_Mot_Enc2.pin2, VCC2.+
  N1: hc-sr1.Trig, Componente1.D14/TX3
  N2: hc-sr1.Echo, Componente1.D15/RX3
  GND: hc-sr1.GND, hc-sr2.GND, hc-sr3.GND, Componente1.GND, IC1.0V, DC_Mot_Enc2.pin6, VCC2.-
  N3: hc-sr2.Trig, Componente1.D18/TX1
  N4: hc-sr2.Echo, Componente1.D19/RX1
  N5: hc-sr3.Trig, Componente1.D16_PWM/TX2
  N6: hc-sr3.Echo, Componente1.D17_PWM/RX2
  N7: Componente1.A8, DC_Mot_Enc2.pin4
  N8: Componente1.A9, DC_Mot_Enc2.pin3
  N9: Componente1.D3_PWM, IC1.In_2
  N10: Componente1.D4_PWM, IC1.In_1
  N11: Componente1.D5_PWM, IC1.Enable_1
  N12: IC1.Out_1_(_Controlled_by_Enable_1_), DC_Mot_Enc2.pin5
  N13: IC1.Out_2_(_Controlled_by_Enable_1_), DC_Mot_Enc2.pin1

notes:
  Pixy2 |
  V

custom parts:
  Battery: Your standard 2x 18650 battery pack (7,4 Volts)
  TRANSCHIPTC5747: CMOS image sensor
  TRANSCHIPTC5747: CMOS image sensor
