# Fritzing sketch DELTA Final electric diagram (saved by Fritzing 0.9.3b)

parts:
  M1 = DOIT Esp32 DevKit v1 (30 pins long, 11 pins width) [part_number=ESP32S-PIN30]  # not connected
  A1 = DORHEA ESP32 GPIO breakout board 30pin
  L298N1 = L298N DC motor driver
  DC_Mot_Enc1 = DC Motor with two-phase hall-encoder [part_number=VT-E-G25A-06-177E]
  BAT1 = 18650 battery holder [package=battery-18650-kit]
  BAT2 = 18650 battery holder [package=battery-18650-kit]  # not connected
  BAT3 = 18650 battery holder [package=battery-18650-kit]
  hc-sr1 = hc-sr04
  hc-sr2 = hc-sr04
  hc-sr3 = hc-sr04
  J1 = Basic Servo  # not connected
  U2 = V_REG_MIC2920 [package=sot223]

nets:
  N1: A1.Pin_6, A1.Pin_7, A1.Pin_45, A1.Pin_46, hc-sr2.Trig
  N2: A1.Pin_8, hc-sr2.Echo
  N3: A1.Pin_9, A1.Pin_10, hc-sr1.Trig, hc-sr1.Echo
  N4: A1.Pin_11, hc-sr3.Echo
  N5: A1.Pin_12, hc-sr3.Trig
  N6: A1.Pin_13, L298N1.ENA
  VCC: A1.Pin_14, A1.Pin_26, A1.Pin_114, hc-sr1.VCC, hc-sr2.VCC, hc-sr3.VCC
  GND: A1.Pin_27, A1.Pin_28, A1.Pin_85, A1.Pin_101, DC_Mot_Enc1.pin5, hc-sr1.GND, hc-sr2.GND, hc-sr3.GND
  N7: A1.Pin_82, DC_Mot_Enc1.pin2
  N8: A1.Pin_117, DC_Mot_Enc1.pin4
  N9: A1.Pin_118, L298N1.IN1
  N10: A1.Pin_119, L298N1.IN2
  N11: A1.Pin_120, DC_Mot_Enc1.pin3
  N12: BAT1.-, U2.IN
  N13: BAT3.+, U2.GND

custom parts:
  DOIT Esp32 DevKit v1 (30 pins long, 11 pins width): The DOIT Esp32 DevKit v1 is one of the development board created by DOIT to evaluate the ESP-WROOM-32 module. It is based on the ESP32 microcontroller that boasts Wifi, Bluetooth, Ethernet and Low Power support all in a single chip. (vanepp) made breadboard work, adjusted pin numbering and labels and reduced size of schematic and cleaned up pcb. This chip is 30pins long (2 x15) and 11 pins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
  DORHEA ESP32 GPIO breakout board 30pin: ESP32 shield 30P expansion board, supports two power supply : DC 6.5-16v and USB 5.V
  L298N DC motor driver: 2x DC motor driver with 78M05 positive voltage regulator (7..35 V) L298N: max 46 V, 2 A Set 5 V Enable jumper to enable 5 V regultor (needed for the L298N) and +5 V output at screw terminal or supply external +5 V at screw terminal Set ENA and/or ENB to +5 V to enable motor permanently or supply ENA and/or ENB with PWM signal IN1 and IN2 set rotation directory for motor A (OUT1/OUT2) IN2 and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
  18650 battery holder: 18650 Battery Holder
